// Logisim project Lab2.circ as structural Verilog
module stack (
  input  Reset,
  input  C,
  input  A0,
  input  A1,
  input  D0,
  input  D1,
  input  D2,
  input  D3,
  output out_9,
  output out_10,
  output out_11,
  output out_12
);

  wire and_1_out, and_2_out, and_3_out, and_4_out, and_5_out, d_ff_1_q, d_ff_2_q, d_ff_3_q, d_ff_4_q,
       decoder_1_out1, decoder_1_out2, decoder_1_out3, increase_modulo_5_1_out_4, increase_modulo_5_1_out_5,
       increase_modulo_5_1_out_6, not_1_out, or_1_out;
  wire [2:0] d_ff_13_q;

  Decoder #(.select(2)) decoder_1 (
    .out1(decoder_1_out1), .out2(decoder_1_out2), .out3(decoder_1_out3), .sel({A1, A0}), .en(C));  // open: out0
  and and_1 (and_1_out, Reset, C);
  not not_1 (not_1_out, and_1_out);
  myJK myjk_1 ();  // open: J, C, K, Q, notQ
  D_Flip_Flop #(.trigger("high")) d_ff_1 (.clk(C), .Q(d_ff_1_q));  // open: D, Qn, preset, reset
  D_Flip_Flop #(.trigger("high")) d_ff_2 (.clk(C), .Q(d_ff_2_q));  // open: D, Qn, preset, reset
  D_Flip_Flop #(.trigger("high")) d_ff_3 (.clk(C), .Q(d_ff_3_q));  // open: D, Qn, preset, reset
  D_Flip_Flop #(.trigger("high")) d_ff_4 (.clk(C), .Q(d_ff_4_q));  // open: D, Qn, preset, reset
  or or_1 (or_1_out, and_1_out, decoder_1_out1);
  D_Flip_Flop #(.trigger("high")) d_ff_5 (.clk(C));  // open: D, Q, Qn, preset, reset
  D_Flip_Flop #(.trigger("high")) d_ff_6 (.clk(C));  // open: D, Q, Qn, preset, reset
  D_Flip_Flop #(.trigger("high")) d_ff_7 (.clk(C));  // open: D, Q, Qn, preset, reset
  D_Flip_Flop #(.trigger("high")) d_ff_8 (.clk(C));  // open: D, Q, Qn, preset, reset
  and and_2 (and_2_out, or_1_out, C);
  D_Flip_Flop #(.trigger("high")) d_ff_9 (.clk(C));  // open: D, Q, Qn, preset, reset
  D_Flip_Flop #(.trigger("high")) d_ff_10 (.clk(C));  // open: D, Q, Qn, preset, reset
  D_Flip_Flop #(.trigger("high")) d_ff_11 (.clk(C));  // open: D, Q, Qn, preset, reset
  D_Flip_Flop #(.trigger("high")) d_ff_12 (.clk(C));  // open: D, Q, Qn, preset, reset
  D_Flip_Flop d_ff_13 (.D(and_3_out), .clk(and_2_out), .Q(d_ff_13_q[0]));  // open: Qn, preset, reset
  D_Flip_Flop d_ff_14 (.D(and_4_out), .clk(and_2_out), .Q(d_ff_13_q[1]));  // open: Qn, preset, reset
  D_Flip_Flop d_ff_15 (.D(and_5_out), .clk(and_2_out), .Q(d_ff_13_q[2]));  // open: Qn, preset, reset
  D_Flip_Flop #(.trigger("high")) d_ff_16 (.clk(C));  // open: D, Q, Qn, preset, reset
  D_Flip_Flop #(.trigger("high")) d_ff_17 (.clk(C));  // open: D, Q, Qn, preset, reset
  D_Flip_Flop #(.trigger("high")) d_ff_18 (.clk(C));  // open: D, Q, Qn, preset, reset
  D_Flip_Flop #(.trigger("high")) d_ff_19 (.clk(C));  // open: D, Q, Qn, preset, reset
  D_Flip_Flop #(.trigger("high")) d_ff_20 (.clk(C));  // open: D, Q, Qn, preset, reset
  D_Flip_Flop #(.trigger("high")) d_ff_21 (.clk(C));  // open: D, Q, Qn, preset, reset
  D_Flip_Flop #(.trigger("high")) d_ff_22 (.clk(C));  // open: D, Q, Qn, preset, reset
  D_Flip_Flop #(.trigger("high")) d_ff_23 (.clk(C));  // open: D, Q, Qn, preset, reset
  Hex_Digit_Display hex_digit_display_1 (.value({1'b0, d_ff_13_q}));  // open: dp
  increase_modulo_5 increase_modulo_5_1 (
    .in_1(d_ff_13_q[0]), .in_2(d_ff_13_q[1]), .in_3(d_ff_13_q[2]), .out_4(increase_modulo_5_1_out_4),
    .out_5(increase_modulo_5_1_out_5), .out_6(increase_modulo_5_1_out_6));
  and and_3 (and_3_out, increase_modulo_5_1_out_4, not_1_out);
  and and_4 (and_4_out, increase_modulo_5_1_out_5, not_1_out);
  and and_5 (and_5_out, increase_modulo_5_1_out_6, not_1_out);
endmodule

module summator (
  input  A,
  input  B,
  input  Cin,
  output S,
  output Cout
);

  wire and_1_out, and_2_out, xor_1_out;

  xor xor_1 (xor_1_out, A, B);
  xor xor_2 (S, xor_1_out, Cin);
  and and_1 (and_1_out, Cin, xor_1_out);
  and and_2 (and_2_out, A, B);
  or or_1 (Cout, and_1_out, and_2_out);
endmodule

module summator3 (
  input  Cin,
  input  A0,
  input  A1,
  input  A2,
  input  B0,
  input  B1,
  input  B2,
  output C0,
  output C1,
  output C2,
  output Cout
);

  wire summator_1_cout, summator_2_cout;

  summator summator_1 (.A(A0), .B(B0), .Cin(Cin), .S(C0), .Cout(summator_1_cout));
  summator summator_2 (.A(A1), .B(B1), .Cin(summator_1_cout), .S(C1), .Cout(summator_2_cout));
  summator summator_3 (.A(A2), .B(B2), .Cin(summator_2_cout), .S(C2), .Cout(Cout));
endmodule

module increase (
  input  in_1,
  input  in_2,
  input  in_3,
  output out_4,
  output out_5,
  output out_6
);

  summator3 summator3_1 (
    .Cin(1'b0), .A0(in_1), .A1(in_2), .A2(in_3), .B0(1'b1), .B1(1'b0), .B2(1'b0), .C0(out_4), .C1(out_5),
    .C2(out_6));  // open: Cout
endmodule

module memory_2 (
  input  in_1,
  input  in_2
);

  Transistor #(.\type ("n")) transistor_1 (.in(in_1), .gate(in_2));  // open: out
endmodule

module increase_modulo_5 (
  input  in_1,
  input  in_2,
  input  in_3,
  output out_4,
  output out_5,
  output out_6
);

  wire increase_1_out_4, increase_1_out_5, increase_1_out_6, nand_1_out, not_1_out;

  increase increase_1 (
    .in_1(in_1), .in_2(in_2), .in_3(in_3), .out_4(increase_1_out_4), .out_5(increase_1_out_5),
    .out_6(increase_1_out_6));
  not not_1 (not_1_out, increase_1_out_5);
  nand nand_1 (nand_1_out, increase_1_out_4, increase_1_out_6);
  and and_1 (out_4, increase_1_out_4, nand_1_out);
  and and_2 (out_5, increase_1_out_5, nand_1_out);
  and and_3 (out_6, increase_1_out_6, nand_1_out);
endmodule

module myJK (
  input  J,
  input  C,
  input  K,
  output Q,
  output notQ
);

  wire nand_1_out, nand_2_out, nand_3_out, nand_4_out, nand_5_out, nand_6_out;

  nand nand_1 (nand_1_out, notQ, J, C);
  nand nand_2 (nand_2_out, C, K, Q);
  nand nand_3 (nand_3_out, nand_1_out, nand_4_out);
  nand nand_4 (nand_4_out, nand_3_out, nand_2_out);
  nand nand_5 (nand_5_out, nand_1_out, nand_3_out);
  nand nand_6 (nand_6_out, nand_4_out, nand_2_out);
  nand nand_7 (Q, nand_5_out, notQ);
  nand nand_8 (notQ, Q, nand_6_out);
endmodule
