// Logisim project not_switch.circ as structural Verilog: 1 circuit, main circuit main
module main (
  input  in,
  output out
);

  Transistor transistor_1 (.in(1'b1), .out(out), .gate(in));
  Transistor #(.\type ("n")) transistor_2 (.in(1'b0), .out(out), .gate(in));

  // Notes on the sheet:
  //   pwr
  //   p1
  //   n1
  //   grd
endmodule
