// Logisim project stack_logical_normal.circ as structural Verilog: 23 circuits, main circuit main
module main (
  input  CLK,
  input  RESET,
  input  [1:0] COMMAND,
  input  [2:0] INDEX,
  input  [3:0] IO_DATA_in,
  output [3:0] IO_DATA_out
);

  stack stack_1 (
    .CLK(CLK), .RESET(RESET), .COMMAND(COMMAND), .INDEX(INDEX), .IO_DATA_IN(IO_DATA_in),
    .IO_DATA_OUT(IO_DATA_out));
endmodule

module stack (
  input  CLK,
  input  RESET,
  input  [1:0] COMMAND,
  input  [2:0] INDEX,
  input  [3:0] IO_DATA_IN,
  output [3:0] IO_DATA_OUT
);

  wire and_1_out, and_2_out, and_3_out, and_4_out, decoder4_1_n1, decoder4_1_n2, decoder4_1_n3, or_1_out;
  wire [2:0] counter_mod5_1_number;
  wire [3:0] memory_1_output_data;

  DECODER4 decoder4_1 (.N(COMMAND), .N1(decoder4_1_n1), .N2(decoder4_1_n2), .N3(decoder4_1_n3));  // open: N0
  and and_1 (and_1_out, CLK, decoder4_1_n1);
  and and_2 (and_2_out, CLK, decoder4_1_n2);
  and and_3 (and_3_out, CLK, decoder4_1_n3);
  // Probe on counter_mod5_1_number
  COUNTER_MOD5 counter_mod5_1 (.INC(decoder4_1_n1), .DEC(decoder4_1_n2), .C(CLK), .NUMBER(counter_mod5_1_number));
  MEMORY memory_1 (
    .INDEX(counter_mod5_1_number), .PUSH(and_1_out), .POP(and_2_out), .GET(and_3_out), .DATA(IO_DATA_IN),
    .GET_INDEX(INDEX), .RESET(RESET), .OUTPUT_DATA(memory_1_output_data));
  and and_4 (and_4_out, CLK, or_1_out);
  or or_1 (or_1_out, decoder4_1_n2, decoder4_1_n3);
  IN_OUT in_out_1 (.IS_OUTPUT(and_4_out), .ODATA(memory_1_output_data), .IDATA(IO_DATA_IN));

  assign IO_DATA_OUT = IO_DATA_IN;

  // Other names for the same wires on the sheet: CLOCK = CLK; IDATA[3:0] = IO_DATA_IN; ODATA[3:0] = IO_DATA_IN

  // Notes on the sheet:
  //   your circuit must be here
endmodule

module D_HIGH (
  input  D,
  input  C,
  output Q,
  output nQ
);

  wire not_1_out;

  not not_1 (not_1_out, D);
  RS_POR rs_por_1 (.R(not_1_out), .C(C), .S(D), .Q(Q), .nQ(nQ));
endmodule

module SUM (
  input  A,
  input  B,
  input  Cin,
  output S,
  output Cout
);

  wire and_1_out, and_2_out, xor_1_out;

  xor xor_1 (xor_1_out, A, B);
  and and_1 (and_1_out, A, B);
  and and_2 (and_2_out, xor_1_out, Cin);
  xor xor_2 (S, xor_1_out, Cin);
  or or_1 (Cout, and_1_out, and_2_out);
endmodule

module SUM3 (
  input  [2:0] A,
  input  [2:0] B,
  output [3:0] C
);

  wire sum_1_cout, sum_2_cout;

  SUM sum_1 (.A(A[0]), .B(B[0]), .Cin(1'b0), .S(C[0]), .Cout(sum_1_cout));
  SUM sum_2 (.A(A[1]), .B(B[1]), .Cin(sum_1_cout), .S(C[1]), .Cout(sum_2_cout));
  SUM sum_3 (.A(A[2]), .B(B[2]), .Cin(sum_2_cout), .S(C[2]), .Cout(C[3]));
endmodule

module COUNTER_MOD5 (
  input  INC,
  input  DEC,
  input  C,
  output [2:0] NUMBER
);

  wire not_1_out, not_2_out, not_3_out;
  wire [2:0] and_2_out, and_3_out, and_4_out, dec_mod5_1_out_2, inc_mod5_1_appmod5, or_1_out;
  wire [2:2] and_1_out;

  not not_1 (not_1_out, C);
  D_FRONT d_front_1 (.D(or_1_out[0]), .C(not_1_out), .Q(NUMBER[0]));  // open: nQ
  D_FRONT d_front_2 (.D(or_1_out[1]), .C(not_1_out), .Q(NUMBER[1]));  // open: nQ
  D_FRONT d_front_3 (.D(or_1_out[2]), .C(not_1_out), .Q(NUMBER[2]));  // open: nQ
  INC_MOD5 inc_mod5_1 (.A(NUMBER), .AppMod5(inc_mod5_1_appmod5));
  DEC_MOD5 dec_mod5_1 (.A(NUMBER), .out_2(dec_mod5_1_out_2));
  not not_2 (not_2_out, INC);
  not not_3 (not_3_out, DEC);
  and and_1 (and_1_out[2], not_2_out, not_3_out);
  assign and_2_out = inc_mod5_1_appmod5 & {3{INC}};  // AND_Gate and_2, 3 bits wide
  assign and_3_out = dec_mod5_1_out_2 & {3{DEC}};  // AND_Gate and_3, 3 bits wide
  assign and_4_out = NUMBER & {3{and_1_out[2]}};  // AND_Gate and_4, 3 bits wide
  assign or_1_out = and_2_out | and_3_out | and_4_out;  // OR_Gate or_1, 3 bits wide
endmodule

module RS_POR (
  input  R,
  input  C,
  input  S,
  output Q,
  output nQ
);

  wire and_1_out, and_2_out, nor_2_out, por_1_out;

  and and_1 (and_1_out, R, C);
  and and_2 (and_2_out, C, S);
  nor nor_1 (Q, and_1_out, nQ);
  nor nor_2 (nor_2_out, Q, and_2_out);
  POR por_1 (.out(por_1_out));
  or or_1 (nQ, nor_2_out, por_1_out);
endmodule

module INC (
  input  [2:0] A,
  output [2:0] App
);

  wire [3:3] sum3_1_c;

  SUM3 sum3_1 (.A(A), .B(3'b001), .C({sum3_1_c[3], App}));
endmodule

module INC_MOD5 (
  input  [2:0] A,
  output [2:0] AppMod5
);

  wire nand_1_out, not_1_out;
  wire [2:0] inc_1_app;

  INC inc_1 (.A(A), .App(inc_1_app));
  not not_1 (not_1_out, inc_1_app[1]);
  nand nand_1 (nand_1_out, inc_1_app[0], not_1_out, inc_1_app[2]);
  and and_1 (AppMod5[0], inc_1_app[0], nand_1_out);
  and and_2 (AppMod5[1], inc_1_app[1], nand_1_out);
  and and_3 (AppMod5[2], inc_1_app[2], nand_1_out);
endmodule

module D_FRONT (
  input  D,
  input  C,
  output Q,
  output nQ
);

  wire d_high_1_q, not_1_out;

  not not_1 (not_1_out, C);
  D_HIGH d_high_1 (.D(D), .C(not_1_out), .Q(d_high_1_q));  // open: nQ
  D_HIGH d_high_2 (.D(d_high_1_q), .C(C), .Q(Q), .nQ(nQ));
endmodule

module DEC_MOD5 (
  input  [2:0] A,
  output [2:0] out_2
);

  wire and_1_out, not_1_out, not_2_out, not_3_out, not_4_out;
  wire [3:0] sum3_1_c;

  not not_1 (not_1_out, A[0]);
  not not_2 (not_2_out, A[1]);
  not not_3 (not_3_out, A[2]);
  and and_1 (and_1_out, not_1_out, not_2_out, not_3_out);
  not not_4 (not_4_out, and_1_out);
  SUM3 sum3_1 (.A(A), .B(3'b111), .C(sum3_1_c));
  and and_2 (out_2[0], not_4_out, sum3_1_c[0]);
  and and_3 (out_2[1], not_4_out, sum3_1_c[1]);
  or or_1 (out_2[2], sum3_1_c[2], and_1_out);
endmodule

module DECODER4 (
  input  [1:0] N,
  output N0,
  output N1,
  output N2,
  output N3
);

  wire not_1_out, not_2_out;

  not not_1 (not_1_out, N[0]);
  not not_2 (not_2_out, N[1]);
  and and_1 (N0, not_1_out, not_2_out);
  and and_2 (N1, N[0], not_2_out);
  and and_3 (N2, N[1], not_1_out);
  and and_4 (N3, N[0], N[1]);
endmodule

module MEMORY_CELL (
  input  [3:0] IDATA,
  input  C,
  output [3:0] ODATA
);

  D_FRONT d_front_1 (.D(IDATA[0]), .C(C), .Q(ODATA[0]));  // open: nQ
  D_FRONT d_front_2 (.D(IDATA[1]), .C(C), .Q(ODATA[1]));  // open: nQ
  D_FRONT d_front_3 (.D(IDATA[2]), .C(C), .Q(ODATA[2]));  // open: nQ
  D_FRONT d_front_4 (.D(IDATA[3]), .C(C), .Q(ODATA[3]));  // open: nQ
endmodule

module DECODER5 (
  input  [2:0] in_1,
  output out_2,
  output out_3,
  output out_4,
  output out_5,
  output out_6
);

  wire not_1_out, not_2_out, not_3_out;

  not not_1 (not_1_out, in_1[0]);
  not not_2 (not_2_out, in_1[1]);
  not not_3 (not_3_out, in_1[2]);
  and and_1 (out_2, not_1_out, not_2_out, not_3_out);
  and and_2 (out_3, in_1[0], not_2_out, not_3_out);
  and and_3 (out_4, not_1_out, in_1[1], not_3_out);
  and and_4 (out_5, in_1[0], in_1[1], not_3_out);
  and and_5 (out_6, not_1_out, not_2_out, in_1[2]);
endmodule

module IF_AND_4 (
  input  in_1,
  input  [3:0] in_2,
  output [3:0] out_3
);

  assign out_3 = {4{in_1}} & in_2;  // AND_Gate and_1, 4 bits wide
endmodule

module DECODER5IF (
  input  [2:0] A,
  input  C,
  output A0,
  output A1,
  output A2,
  output A3,
  output A4
);

  wire decoder5_1_out_2, decoder5_1_out_3, decoder5_1_out_4, decoder5_1_out_5, decoder5_1_out_6;

  DECODER5 decoder5_1 (
    .in_1(A), .out_2(decoder5_1_out_2), .out_3(decoder5_1_out_3), .out_4(decoder5_1_out_4),
    .out_5(decoder5_1_out_5), .out_6(decoder5_1_out_6));
  and and_1 (A0, decoder5_1_out_2, C);
  and and_2 (A1, decoder5_1_out_3, C);
  and and_3 (A2, decoder5_1_out_4, C);
  and and_4 (A3, decoder5_1_out_5, C);
  and and_5 (A4, decoder5_1_out_6, C);
endmodule

module MEMORY (
  input  [2:0] INDEX,
  input  PUSH,
  input  POP,
  input  GET,
  input  [3:0] DATA,
  input  [2:0] GET_INDEX,
  input  RESET,
  output [3:0] OUTPUT_DATA
);

  wire and_1_out, decoder5if_1_a0, decoder5if_1_a1, decoder5if_1_a2, decoder5if_1_a3, decoder5if_1_a4,
       decoder5if_2_a0, decoder5if_2_a1, decoder5if_2_a2, decoder5if_2_a3, decoder5if_2_a4, decoder5if_3_a0,
       decoder5if_3_a1, decoder5if_3_a2, decoder5if_3_a3, decoder5if_3_a4, not_1_out, or_1_out, or_2_out,
       or_3_out, or_4_out, or_5_out, or_6_out, or_7_out, or_8_out, or_9_out, or_10_out;
  wire [2:0] dec_mod5_1_out_2, sub_mod5_1_c;
  wire [3:0] if_and_4_1_out_3, if_and_4_2_out_3, if_and_4_3_out_3, if_and_4_4_out_3, if_and_4_5_out_3,
       if_and_4_6_out_3, memory_cell_1_odata, memory_cell_2_odata, memory_cell_3_odata, memory_cell_4_odata,
       memory_cell_5_odata, not_2_out;

  not not_1 (not_1_out, RESET);
  assign not_2_out = ~if_and_4_1_out_3;  // NOT_Gate not_2, 4 bits wide
  and and_1 (and_1_out, not_2_out[0], not_2_out[1], not_2_out[2], not_2_out[3], RESET);
  DEC_MOD5 dec_mod5_1 (.A(INDEX), .out_2(dec_mod5_1_out_2));
  DECODER5IF decoder5if_1 (
    .A(INDEX), .C(PUSH), .A0(decoder5if_1_a0), .A1(decoder5if_1_a1), .A2(decoder5if_1_a2),
    .A3(decoder5if_1_a3), .A4(decoder5if_1_a4));
  // Probe on if_and_4_1_out_3
  IF_AND_4 if_and_4_1 (.in_1(not_1_out), .in_2(DATA), .out_3(if_and_4_1_out_3));
  or or_1 (or_1_out, decoder5if_1_a0, and_1_out);
  or or_2 (or_2_out, decoder5if_1_a1, and_1_out);
  or or_3 (or_3_out, decoder5if_1_a2, and_1_out);
  or or_4 (or_4_out, decoder5if_1_a3, and_1_out);
  or or_5 (or_5_out, decoder5if_1_a4, and_1_out);
  SUB_MOD5 sub_mod5_1 (.A(INDEX), .B(GET_INDEX), .C(sub_mod5_1_c));
  DECODER5IF decoder5if_2 (
    .A(dec_mod5_1_out_2), .C(POP), .A0(decoder5if_2_a0), .A1(decoder5if_2_a1), .A2(decoder5if_2_a2),
    .A3(decoder5if_2_a3), .A4(decoder5if_2_a4));
  // Probe on memory_cell_1_odata
  MEMORY_CELL memory_cell_1 (.IDATA(if_and_4_1_out_3), .C(or_1_out), .ODATA(memory_cell_1_odata));
  // Probe on memory_cell_2_odata
  MEMORY_CELL memory_cell_2 (.IDATA(if_and_4_1_out_3), .C(or_2_out), .ODATA(memory_cell_2_odata));
  // Probe on memory_cell_3_odata
  MEMORY_CELL memory_cell_3 (.IDATA(if_and_4_1_out_3), .C(or_3_out), .ODATA(memory_cell_3_odata));
  // Probe on memory_cell_4_odata
  MEMORY_CELL memory_cell_4 (.IDATA(if_and_4_1_out_3), .C(or_4_out), .ODATA(memory_cell_4_odata));
  // Probe on memory_cell_5_odata
  MEMORY_CELL memory_cell_5 (.IDATA(if_and_4_1_out_3), .C(or_5_out), .ODATA(memory_cell_5_odata));
  DECODER5IF decoder5if_3 (
    .A(sub_mod5_1_c), .C(GET), .A0(decoder5if_3_a0), .A1(decoder5if_3_a1), .A2(decoder5if_3_a2),
    .A3(decoder5if_3_a3), .A4(decoder5if_3_a4));
  or or_6 (or_6_out, decoder5if_2_a0, decoder5if_3_a0);
  or or_7 (or_7_out, decoder5if_2_a1, decoder5if_3_a1);
  or or_8 (or_8_out, decoder5if_2_a2, decoder5if_3_a2);
  or or_9 (or_9_out, decoder5if_2_a3, decoder5if_3_a3);
  or or_10 (or_10_out, decoder5if_2_a4, decoder5if_3_a4);
  IF_AND_4 if_and_4_2 (.in_1(or_6_out), .in_2(memory_cell_1_odata), .out_3(if_and_4_2_out_3));
  IF_AND_4 if_and_4_3 (.in_1(or_7_out), .in_2(memory_cell_2_odata), .out_3(if_and_4_3_out_3));
  IF_AND_4 if_and_4_4 (.in_1(or_8_out), .in_2(memory_cell_3_odata), .out_3(if_and_4_4_out_3));
  IF_AND_4 if_and_4_5 (.in_1(or_9_out), .in_2(memory_cell_4_odata), .out_3(if_and_4_5_out_3));
  IF_AND_4 if_and_4_6 (.in_1(or_10_out), .in_2(memory_cell_5_odata), .out_3(if_and_4_6_out_3));
  // Probe on if_and_4_2_out_3
  // Probe on if_and_4_3_out_3
  // Probe on if_and_4_4_out_3
  // Probe on if_and_4_5_out_3
  // Probe on if_and_4_6_out_3
  assign OUTPUT_DATA = if_and_4_2_out_3 | if_and_4_3_out_3 | if_and_4_4_out_3 | if_and_4_5_out_3 | if_and_4_6_out_3;  // OR_Gate or_11, 4 bits wide
endmodule

module SUB_MOD5 (
  input  [2:0] A,
  input  [2:0] B,
  output [2:0] C
);

  wire [2:0] invert5_1_na, mod5_1_number_out;
  wire [3:0] sum3_1_c;

  // Probe on invert5_1_na
  INVERT5 invert5_1 (.A(B), .nA(invert5_1_na));
  SUM3 sum3_1 (.A(A), .B(invert5_1_na), .C(sum3_1_c));
  MOD5 mod5_1 (.NUMBER_IN(sum3_1_c), .NUMBER_OUT(mod5_1_number_out));
  INC_MOD5 inc_mod5_1 (.A(mod5_1_number_out), .AppMod5(C));
endmodule

module MOD5 (
  input  [3:0] NUMBER_IN,
  output [2:0] NUMBER_OUT
);

  wire and_1_out, and_2_out, and_3_out, and_4_out, and_5_out, and_6_out, and_7_out, and_8_out, and_9_out,
       and_10_out, and_11_out, and_12_out, and_13_out, and_14_out, and_15_out, and_16_out, or_2_out,
       or_3_out, or_4_out;
  wire [3:0] not_1_out;

  assign not_1_out = ~NUMBER_IN;  // NOT_Gate not_1, 4 bits wide
  and and_1 (and_1_out, not_1_out[0], not_1_out[1], not_1_out[2], not_1_out[3]);
  and and_2 (and_2_out, NUMBER_IN[0], not_1_out[1], not_1_out[2], not_1_out[3]);
  and and_3 (and_3_out, not_1_out[0], NUMBER_IN[1], not_1_out[2], not_1_out[3]);
  and and_4 (and_4_out, NUMBER_IN[0], NUMBER_IN[1], not_1_out[2], not_1_out[3]);
  and and_5 (and_5_out, not_1_out[0], not_1_out[1], NUMBER_IN[2], not_1_out[3]);
  and and_6 (and_6_out, NUMBER_IN[0], not_1_out[1], NUMBER_IN[2], not_1_out[3]);
  and and_7 (and_7_out, not_1_out[0], NUMBER_IN[1], NUMBER_IN[2], not_1_out[3]);
  and and_8 (and_8_out, NUMBER_IN[0], NUMBER_IN[1], NUMBER_IN[2], not_1_out[3]);
  and and_9 (and_9_out, not_1_out[0], not_1_out[1], not_1_out[2], NUMBER_IN[3]);
  and and_10 (and_10_out, NUMBER_IN[0], not_1_out[1], not_1_out[2], NUMBER_IN[3]);
  and and_11 (and_11_out, not_1_out[0], NUMBER_IN[1], not_1_out[2], NUMBER_IN[3]);
  and and_12 (and_12_out, NUMBER_IN[0], NUMBER_IN[1], not_1_out[2], NUMBER_IN[3]);
  and and_13 (and_13_out, not_1_out[0], not_1_out[1], NUMBER_IN[2], NUMBER_IN[3]);
  and and_14 (and_14_out, NUMBER_IN[0], not_1_out[1], NUMBER_IN[2], NUMBER_IN[3]);
  and and_15 (and_15_out, not_1_out[0], NUMBER_IN[1], NUMBER_IN[2], NUMBER_IN[3]);
  and and_16 (and_16_out, NUMBER_IN[0], NUMBER_IN[1], NUMBER_IN[2], NUMBER_IN[3]);
  // OR_Gate or_1 has open pins: in0=and_1_out, in1=and_6_out, in2=and_11_out, in3=and_16_out, out=open
  or or_2 (or_2_out, and_2_out, and_7_out, and_12_out);
  or or_3 (or_3_out, and_3_out, and_8_out, and_13_out);
  or or_4 (or_4_out, and_4_out, and_9_out, and_14_out);
  or or_5 (NUMBER_OUT[2], and_5_out, and_10_out, and_15_out);
  or or_6 (NUMBER_OUT[0], or_2_out, or_4_out);
  or or_7 (NUMBER_OUT[1], or_3_out, or_4_out);
endmodule

module INVERT5 (
  input  [2:0] A,
  output [2:0] nA
);

  wire and_2_out, and_3_out, and_4_out, and_5_out;
  wire [2:0] mod5_1_number_out, not_1_out;

  MOD5 mod5_1 (.NUMBER_IN({1'b0, A}), .NUMBER_OUT(mod5_1_number_out));
  assign not_1_out = ~mod5_1_number_out;  // NOT_Gate not_1, 3 bits wide
  and and_1 (nA[2], not_1_out[0], not_1_out[1], not_1_out[2]);
  and and_2 (and_2_out, mod5_1_number_out[0], not_1_out[1], not_1_out[2]);
  and and_3 (and_3_out, not_1_out[0], mod5_1_number_out[1], not_1_out[2]);
  and and_4 (and_4_out, mod5_1_number_out[0], mod5_1_number_out[1], not_1_out[2]);
  and and_5 (and_5_out, not_1_out[0], not_1_out[1], mod5_1_number_out[2]);
  or or_1 (nA[0], and_2_out, and_4_out);
  or or_2 (nA[1], and_2_out, and_3_out);
endmodule

module IN_OUT (
  input  IS_OUTPUT,
  input  [3:0] ODATA,
  output [3:0] IDATA
);

  wire not_1_out;

  not not_1 (not_1_out, IS_OUTPUT);
  // Transmission_Gate transmission_1: pin names not known; wires that end beside it: ODATA[0], not_1_out, IS_OUTPUT, IDATA[0]
  // Transmission_Gate transmission_2: pin names not known; wires that end beside it: ODATA[1], not_1_out, IS_OUTPUT, IDATA[1]
  // Transmission_Gate transmission_3: pin names not known; wires that end beside it: ODATA[2], not_1_out, IS_OUTPUT, IDATA[2]
  // Transmission_Gate transmission_4: pin names not known; wires that end beside it: ODATA[3], not_1_out, IS_OUTPUT, IDATA[3]
endmodule

module COUNTER_MOD5_WITH_RESET (
  input  INC,
  input  DEC,
  input  C,
  input  R,
  output [2:0] NUMBER
);

  wire not_1_out, not_2_out;
  wire [2:0] and_2_out, and_3_out, and_4_out, dec_mod5_1_out_2, inc_mod5_1_appmod5, or_1_out;
  wire [2:2] and_1_out;

  D_RESET d_reset_1 (.D(or_1_out[0]), .C(C), .R(R), .Q(NUMBER[0]));  // open: nQ
  D_RESET d_reset_2 (.D(or_1_out[1]), .C(C), .R(R), .Q(NUMBER[1]));  // open: nQ
  D_RESET d_reset_3 (.D(or_1_out[2]), .C(C), .R(R), .Q(NUMBER[2]));  // open: nQ
  INC_MOD5 inc_mod5_1 (.A(NUMBER), .AppMod5(inc_mod5_1_appmod5));
  DEC_MOD5 dec_mod5_1 (.A(NUMBER), .out_2(dec_mod5_1_out_2));
  not not_1 (not_1_out, INC);
  not not_2 (not_2_out, DEC);
  and and_1 (and_1_out[2], not_1_out, not_2_out);
  assign and_2_out = inc_mod5_1_appmod5 & {3{INC}};  // AND_Gate and_2, 3 bits wide
  assign and_3_out = dec_mod5_1_out_2 & {3{DEC}};  // AND_Gate and_3, 3 bits wide
  assign and_4_out = NUMBER & {3{and_1_out[2]}};  // AND_Gate and_4, 3 bits wide
  assign or_1_out = and_2_out | and_3_out | and_4_out;  // OR_Gate or_1, 3 bits wide
endmodule

module D_RESET (
  input  D,
  input  C,
  input  R,
  output Q,
  output nQ
);

  wire and_1_out, and_2_out, d_high_1_q, not_1_out, not_2_out, not_3_out, or_1_out, or_2_out;

  not not_1 (not_1_out, R);
  and and_1 (and_1_out, D, not_1_out);
  or or_1 (or_1_out, R, not_2_out);
  not not_2 (not_2_out, C);
  D_HIGH d_high_1 (.D(and_1_out), .C(or_1_out), .Q(d_high_1_q));  // open: nQ
  not not_3 (not_3_out, R);
  and and_2 (and_2_out, d_high_1_q, not_3_out);
  or or_2 (or_2_out, C, R);
  D_HIGH d_high_2 (.D(and_2_out), .C(or_2_out), .Q(Q), .nQ(nQ));
endmodule
